// Logisim project CPU.circ as structural Verilog: 1 circuit, main circuit main
module main (
  input  Clock
);

  wire [4:0] Clock_Tracker_out_2;

  Fetch Fetch (.Clock(Clock));  // open: Instructions, Clock_2
  Clock Clock_Tracker (.Clock(Clock), .out_2(Clock_Tracker_out_2));
endmodule
